# Fritzing sketch Project1 (saved by Fritzing 0.9.10b)
breadboards: 1

parts:
  Part1 = Arduino Nano (Rev3.0) (ICSP)
  LED1 = smd LED [color="Yellow (595nm)" package="1206 [SMD]"]
  R1 = Resistor [tolerance=±5% resistance=10k package="0805 [SMD]"]
  R2 = Resistor [tolerance=±5% resistance=10k package="0805 [SMD]"]
  HC-SR04_Sensor_1 = HC-SR04 Ultrasonic Distance Sensor
  S1 = SPST Switch [package=switch-spdt_lock.007s]
  R3 = Resistor [tolerance=±5% resistance=10k package="0805 [SMD]"]
  R4 = Resistor [tolerance=±5% resistance=220 package="0805 [SMD]"]
  R5 = Resistor [tolerance=±5% resistance=220 package="0805 [SMD]"]
  R6 = Resistor [tolerance=±5% resistance=220 package="0805 [SMD]"]
  LED2 = smd LED [color="Yellow (595nm)" package="1206 [SMD]"]
  LED3 = smd LED [color="Yellow (595nm)" package="1206 [SMD]"]

nets:
  GND: Part1.GND, R1.Pin_1, HC-SR04_Sensor_1.GND, R3.Pin_0, R4.Pin_1, R5.Pin_1, R6.Pin_1
  N1: Part1.D2, R1.Pin_0, R2.Pin_1
  N2: Part1.D3, HC-SR04_Sensor_1.TRIG
  N3: Part1.D5, LED1.cathode
  N4: Part1.D6, LED2.cathode
  N5: Part1.D7, LED3.cathode
  N6: Part1.D9, R3.Pin_1
  N7: Part1.3V3, S1.O
  N8: LED1.anode, R4.Pin_0
  N9: R2.Pin_0, HC-SR04_Sensor_1.ECHO
  N10: R5.Pin_0, LED2.anode
  N11: R6.Pin_0, LED3.anode
